# Fritzing sketch alu_flags (saved by Fritzing 0.9.3b)
stripboards: 1

parts:
  IC1 = IC, DIP package, 20 pins [chip_label="Transceiver (245)"]
  J1 = female pin header, 2 pins [form="♀ (female)"]  # not connected
  J2 = female pin header, 2 pins [form="♀ (female)"]  # not connected
  J3 = female pin header, 2 pins [form="♀ (female)"]  # not connected
  J4 = female pin header, 2 pins [form="♀ (female)"]  # not connected
  J5 = female pin header, 2 pins [form="♀ (female)"]  # not connected
  J6 = female pin header, 2 pins [form="♀ (female)"]  # not connected
  J7 = female pin header, 2 pins [form="♀ (female)"]  # not connected
  J8 = female pin header, 2 pins [form="♀ (female)"]  # not connected
  IC2 = IC, DIP package, 16 pins [chip_label="Register (173)"]
  IC4 = IC, DIP package, 14 pins [chip_label="4in AND (21)"]
  J9 = female pin header, 2 pins [form="♀ (female)"]
  J11 = female pin header, 2 pins [form="♀ (female)"]
  J12 = female pin header, 2 pins [form="♀ (female)"]
  J13 = female pin header, 2 pins [form="♀ (female)"]
  J14 = female pin header, 2 pins [form="♀ (female)"]
  J15 = female pin header, 2 pins [form="♀ (female)"]
  J16 = female pin header, 2 pins [form="♀ (female)"]
  IC5 = IC, DIP package, 14 pins [chip_label="2in NOR (02)"]
  J24 = female pin header, 1 pin [form="♀ (female)"]
  J26 = female pin header, 1 pin [form="♀ (female)"]  # not connected
  J28 = female pin header, 2 pins [form="♀ (female)"]  # not connected
  J10 = female pin header, 2 pins [form="♀ (female)"]
  LED1 = LED - 5mm [color="Red (633nm)" package="5 mm [THT]"]
  LED2 = LED - 5mm [color="Green (560nm)" package="5 mm [THT]"]

nets:
  N1: IC1.pin1, IC1.pin9, IC1.pin12, IC1.pin20, IC2.pin7, IC2.pin10, IC4.pin7, IC4.pin8, J14.pin2, IC5.pin7, IC5.pin8, J24.pin1, J10.pin1
  N2: IC1.pin2, IC1.pin19, IC2.pin8, IC2.pin9
  N3: IC1.pin3, IC1.pin18, IC2.pin1, IC2.pin16, IC4.pin1, IC4.pin14, J12.pin1, IC5.pin1, IC5.pin14, LED1.cathode
  N4: IC1.pin4, IC1.pin10, IC1.pin11, IC1.pin17, IC2.pin4, IC2.pin13, IC4.pin4, IC4.pin11, J12.pin2, J16.pin1, IC5.pin2, IC5.pin13, J10.pin2
  N5: IC1.pin5, IC1.pin16, J11.pin1, J13.pin1, J16.pin2, IC5.pin3, IC5.pin12, LED2.cathode
  N6: IC1.pin6, IC1.pin15, IC2.pin2, IC2.pin15, IC4.pin2, IC4.pin13, J11.pin2, J13.pin2, IC5.pin4, IC5.pin11, LED1.anode, LED2.anode
  N7: IC1.pin7, IC1.pin14, IC2.pin5, IC2.pin12, IC4.pin5, IC4.pin10, J9.pin1, J15.pin1, IC5.pin5, IC5.pin10
  N8: IC1.pin8, IC1.pin13, J9.pin2, J14.pin1, J15.pin2, IC5.pin6, IC5.pin9
  N9: IC2.pin3, IC2.pin14, IC4.pin3, IC4.pin12
  N10: IC2.pin6, IC2.pin11, IC4.pin6, IC4.pin9

notes:
  0V
  +ve
  To Flags
  Transceiver to bus. LEDs. Status register + status LEDs. Status out.
  To bus
  ALU out, carry bit
  Out to bus
