# Fritzing sketch ir (saved by Fritzing 0.9.4)
stripboards: 1

parts:
  LED1 = LED - 3mm [color="Red (633nm)" package="3 mm [THT]"]
  LED2 = LED - 3mm [color="Red (633nm)" package="3 mm [THT]"]
  LED3 = LED - 3mm [color="Red (633nm)" package="3 mm [THT]"]
  LED4 = LED - 3mm [color="Red (633nm)" package="3 mm [THT]"]
  LED5 = LED - 3mm [color="Red (633nm)" package="3 mm [THT]"]
  LED6 = LED - 3mm [color="Red (633nm)" package="3 mm [THT]"]
  LED7 = LED - 3mm [color="Red (633nm)" package="3 mm [THT]"]
  LED8 = LED - 3mm [color="Red (633nm)" package="3 mm [THT]"]
  J1 = female pin header, 2 pins [form="♀ (female)"]
  J2 = female pin header, 2 pins [form="♀ (female)"]
  J3 = female pin header, 2 pins [form="♀ (female)"]
  J4 = female pin header, 2 pins [form="♀ (female)"]
  IC2 = IC, DIP package, 16 pins [chip_label="4-bit reg"]
  IC3 = IC, DIP package, 16 pins [chip_label="4-bit reg"]
  J5 = female pin header, 2 pins [form="♀ (female)"]
  J6 = female pin header, 2 pins [form="♀ (female)"]
  J7 = female pin header, 2 pins [form="♀ (female)"]
  J8 = female pin header, 2 pins [form="♀ (female)"]

nets:
  N1: LED1.cathode, J1.pin1, IC3.pin3
  N2: LED1.anode, LED2.anode, LED3.anode, LED4.anode, IC2.pin1, IC2.pin2, IC2.pin8, IC3.pin1, IC3.pin2, IC3.pin8
  N3: LED2.cathode, J1.pin2, IC3.pin4
  N4: LED3.cathode, J2.pin1, IC3.pin5
  N5: LED4.cathode, J2.pin2, IC3.pin6
  N6: LED5.cathode, J3.pin1, IC2.pin3
  N7: LED5.anode, LED6.anode, LED7.anode, LED8.anode, IC2.pin7, IC3.pin7
  N8: LED6.cathode, J3.pin2, IC2.pin4
  N9: LED7.cathode, J4.pin1, IC2.pin5
  N10: LED8.cathode, J4.pin2, IC2.pin6
  N11: IC2.pin9, IC2.pin10, IC3.pin9, IC3.pin10
  N12: IC2.pin11, J7.pin2
  N13: IC2.pin12, J7.pin1
  N14: IC2.pin13, J8.pin2
  N15: IC2.pin14, J8.pin1
  N16: IC2.pin15, IC3.pin15
  N17: IC2.pin16, IC3.pin16
  N18: IC3.pin11, J6.pin2
  N19: IC3.pin12, J6.pin1
  N20: IC3.pin13, J5.pin2
  N21: IC3.pin14, J5.pin1

notes:
  0V
  +ve
  To microcontroller
  To bus
  Reset
  !Load
  Clock
